# Fritzing sketch schematic (saved by Fritzing 0.9.3b)
breadboards: 1

parts:
  S1 = Momentary Switch [package=ksa_sealed_tac_switch]  # not connected
  Raspberry_Pi1 = Raspberry Pi B rev2
  LED3 = LED - 5mm [color="Blue (525nm)" package="5 mm [THT]"]
  R3 = Resistor [tolerance=±5% resistance=220 package="2010 [SMD]"]
  R5 = Resistor [tolerance=±5% resistance=10k package="2010 [SMD]"]

nets:
  N1: Raspberry_Pi1.GND, R3.Pin_1, R5.Pin_1
  N2: Raspberry_Pi1.GPIO_17, LED3.anode
  N3: LED3.cathode, R3.Pin_0
